# Fritzing sketch rgb_led_intro (saved by Fritzing 0.9.3b)
breadboards: 1

parts:
  LED1 = RGB LED (com. cathode, rgb) [package="5 mm [THT]"]
  R1 = Resistor [tolerance=±5% resistance=220 package=THT]
  R2 = Resistor [tolerance=±5% resistance=220 package=THT]
  R3 = Resistor [tolerance=±5% resistance=220 package=THT]
  Part1 = Arduino Uno (Rev3)

nets:
  N1: LED1.red_anode, R2.Pin_0
  N2: LED1.green_anode, R1.Pin_0
  N3: LED1.blue_anode, R3.Pin_0
  N4: R1.Pin_1, Part1.D10_PWM/SS
  N5: R2.Pin_1, Part1.D11_PWM/MOSI
  N6: R3.Pin_1, Part1.D9_PWM
